# Fritzing sketch anti_rebound (saved by Fritzing 0.8.0b)
breadboards: 1

parts:
  Parte1 = Arduino Uno (Rev3)
  R1 = Resistor [tolerance=±5% resistance=150 package=THT]
  R2 = Resistor [tolerance=±5% resistance=150 package=THT]
  LED1 = LED - 5mm [color="Red (635nm)" package="5 mm [THT]"]
  LED2 = LED - 5mm [color="Red (635nm)" package="5 mm [THT]"]
  D1 = Rectifier Diode [part_number=1N4001 package="300 mil [THT]"]
  S1 = Pushbutton [package=THT]
  R4 = Resistor [tolerance=±5% resistance=4.7 package="0603 [SMD]"]
  R3 = Resistor [tolerance=±5% resistance=150 package="0603 [SMD]"]
  C1 = Ceramic Capacitor [capacitance=100nF package="1206 [SMD, multilayer]"]

nets:
  N1: Parte1.GND, LED1.cathode, LED2.cathode, S1.leg0, C1.0
  N2: Parte1.5V, R3.Pin_1
  N3: Parte1.D9_PWM, R2.Pin_1
  N4: Parte1.D10_PWM/SS, R1.Pin_1
  N5: Parte1.D2, D1.cathode, R4.Pin_1, C1.1
  N6: R1.Pin_0, LED2.anode
  N7: R2.Pin_0, LED1.anode
  N8: D1.anode, S1.leg1, R4.Pin_0, R3.Pin_0
