# Fritzing sketch schema (saved by Fritzing 0.8.0b)
breadboards: 1

parts:
  LED1 = LED - 3mm [color="Green (560nm)" package="3 mm [THT]"]
  LED2 = LED - 3mm [color="Red (633nm)" package="3 mm [THT]"]
  R2 = Resistor [tolerance=±5% resistance=150 package="0805 [SMD]"]
  R1 = Resistor [tolerance=±5% resistance=150 package="0805 [SMD]"]
  S2 = Round Pushbutton
  Parte1 = Arduino Uno (Rev3)
  R3 = Resistor [tolerance=±5% resistance=150 package="0603 [SMD]"]

nets:
  N1: LED1.cathode, LED2.cathode, S2.leg0, S2.leg1, Parte1.GND, Parte1.D2, R3.Pin_0
  N2: LED1.anode, R2.Pin_1
  N3: LED2.anode, R1.Pin_1
  N4: R2.Pin_0, Parte1.D10_PWM/SS
  N5: R1.Pin_0, Parte1.D9_PWM
  N6: Parte1.5V, R3.Pin_1
